# Fritzing sketch car (saved by Fritzing 0.9.3b)

parts:
  Часть1 = Arduino Uno (Rev3)
  S1 = H-Bridge with L298N
  M1 = DC Motor
  M2 = DC Motor
  Часть2 = Bluetooth HC-06
  VCC1 = Battery block 9V

nets:
  N1: Часть1.D8, Часть2.TXD
  N2: Часть1.D9_PWM, Часть2.RXD
  GND: Часть1.GND, S1.GND, Часть2.GND, VCC1.-
  N3: Часть1.D2, S1.ENA
  N4: Часть1.D3_PWM, S1.IN1
  N5: Часть1.D4, S1.IN2
  N6: Часть1.D5_PWM, S1.IN3
  N7: Часть1.D6_PWM, S1.IN4
  N8: Часть1.D7, S1.ENB
  N9: Часть1.ioref, S1.5V
  5V: Часть1.5V, Часть2.VCC
  N10: S1.12V, VCC1.+
  N11: S1.M1-01, M2.pin_2
  N12: S1.M1-02, M2.pin_1
  N13: S1.M2-01, M1.pin_1
  N14: S1.M2-02, M1.pin_2

custom parts:
  H-Bridge with L298N: h-bridge

// code stored in the sketch: car.ino
/**
* @link https://github.com/Almadef/car/
* @copyright Copyright (c) 2019 Chuvashov Mikhail
* @license https://github.com/Almadef/car/blob/master/LICENSE
*/

// Connecting Bluetooth library
#include <SoftwareSerial.h>

// Driving motor (Motor A) pins
#define ROTATION_MOTOR_A_1 3
#define ROTATION_MOTOR_A_2 4
#define SPEED_MOTOR_A 2

// Rotating motor (Motor B) pins
#define ROTATION_MOTOR_B_1 5
#define ROTATION_MOTOR_B_2 6
#define SPEED_MOTOR_B 7

// Bluetooth pins
#define TxD 8
#define RxD 9

SoftwareSerial bluetoothSerial(TxD, RxD);

char c;

void setup()
{
    bluetoothSerial.begin(9600);
    Serial.begin(9600);
    pinMode(ROTATION_MOTOR_A_1, OUTPUT);
    pinMode(ROTATION_MOTOR_A_2, OUTPUT);
    pinMode(SPEED_MOTOR_A, OUTPUT);
    pinMode(ROTATION_MOTOR_B_1, OUTPUT);
    pinMode(ROTATION_MOTOR_B_2, OUTPUT);
    pinMode(SPEED_MOTOR_B, OUTPUT);  
}

void loop()
{
    if (bluetoothSerial.available())
    {
        c = bluetoothSerial.read();
        Serial.println(c);
        if (c == '0')
        {
            // Stop motors
            analogWrite(SPEED_MOTOR_A, 0);
            analogWrite(SPEED_MOTOR_B, 0);
        }
        if (c == '1')
        {
            // Motor B left
            analogWrite(SPEED_MOTOR_B, 255);
            digitalWrite(ROTATION_MOTOR_B_1, HIGH);
            digitalWrite(ROTATION_MOTOR_B_2, LOW);
        }
        if (c == '2')
        {
            // Motor B right
            analogWrite(SPEED_MOTOR_B, 255);
            digitalWrite(ROTATION_MOTOR_B_1, LOW);
            digitalWrite(ROTATION_MOTOR_B_2, HIGH);
        }
        if (c == '3')
        {
            // Motor A up
            analogWrite(SPEED_MOTOR_A, 255);
            digitalWrite(ROTATION_MOTOR_A_1, LOW);
            digitalWrite(ROTATION_MOTOR_A_2, HIGH);
        }
        if (c == '4')
        {
            // Motor A down
            analogWrite(SPEED_MOTOR_A, 255);
            digitalWrite(ROTATION_MOTOR_A_1, HIGH);
            digitalWrite(ROTATION_MOTOR_A_2, LOW);
        }
    }
}
